# Fritzing sketch AquaFish (saved by Fritzing 0.9.3b)
breadboards: 1

parts:
  Heltec_WiFi_LoRa_1 = Heltec WiFi LoRa 32 [part_number=HTIT-WB32LA]
  LCD2004-I2C1 = LCD2004-I2C
  DS1 = DS18B20 1-Wire Temperature Sensor [part_number=DS18B20]
  A1 = tds-sensor-meter-v1.0_1
  S1 = PH meter [package=THT]
  R1 = Resistor [tolerance=±5% resistance=220 package=THT]

nets:
  N1: Heltec_WiFi_LoRa_1.pin_1, LCD2004-I2C1.SDA
  N2: Heltec_WiFi_LoRa_1.pin_14, A1.pin1
  N3: Heltec_WiFi_LoRa_1.pin_15, S1.pin1
  N4: Heltec_WiFi_LoRa_1.pin_16, Heltec_WiFi_LoRa_1.pin_21
  N5: Heltec_WiFi_LoRa_1.pin_17, Heltec_WiFi_LoRa_1.pin_20, LCD2004-I2C1.VCC, A1.pin2, S1.pin2, R1.Pin_0
  GND: Heltec_WiFi_LoRa_1.pin_18, Heltec_WiFi_LoRa_1.pin_19, Heltec_WiFi_LoRa_1.pin_22, LCD2004-I2C1.GND, DS1.GND, A1.pin3, S1.pin3
  N6: Heltec_WiFi_LoRa_1.pin_27, LCD2004-I2C1.SCL
  N7: Heltec_WiFi_LoRa_1.pin_29, DS1.DQ
  N8: DS1.VDD, R1.Pin_1

custom parts:
  Heltec WiFi LoRa 32: Heltec WiFi LoRa 32 WiFi LoRa 32 is a classic IoT dev-board designed & produced by Heltec Automation(TM). It’s a highly integrated product based on ESP32 + SX127x, it has Wi-Fi, BLE, LoRa functions, also Li-Po battery management system, 0.96″ OLED are also included. It’s the best choice for smart cities, smart farms, smart home, and IoT makers.
  LCD2004-I2C: A standard character display with 4x20 characters. Comes in many colors with LCM2004 IIC attached.
  : TDS Meter V1.0 Development Board Water Meter Filter Measuring Water Sensor Module.
